# Fritzing sketch Bluetooth (saved by Fritzing 0.9.2b)
breadboards: 1

parts:
  パーツ1 = Arduino Uno (Rev3)
  パーツ2 = Bluetooth Module Breakout - Roving Networks (RN-41)
  R1 = Resistor [tolerance=±5% resistance=1.8k package=THT]
  R2 = Resistor [tolerance=±5% resistance=1.8k package=THT]

nets:
  GND: パーツ1.GND, パーツ2.GND, R2.Pin_1
  N1: パーツ1.D0/RX, パーツ2.UARTTX
  N2: パーツ1.D1/TX, R1.Pin_0
  3V3: パーツ1.3V3, パーツ2.VCC
  N3: パーツ2.UARTCTS, パーツ2.UARTRTS
  N4: パーツ2.UARTRX, R1.Pin_1, R2.Pin_0
