# Fritzing sketch MotorControl (saved by Fritzing 0.9.2b)
breadboards: 1

parts:
  Arduino1 = Arduino Uno (Rev3)
  IC1 = IC, SIP package, 7 pins [chip_label=TA8428K]
  F1 = Resettable Fuse PTC [package=ptc]
  C1 = Electrolytic Capacitor [capacitance=10µF voltage=50V package="100 mil [THT, electrolytic]"]
  C2 = Ceramic Capacitor [capacitance=100nF package="100 mil [THT, multilayer]"]
  J1 = Screw terminal - 2 pins [package=THT]
  LED1 = LED - 5mm [color="Red (633nm)" package="5 mm [THT]"]
  LED2 = LED - 5mm [color="Green (560nm)" package="5 mm [THT]"]
  R1 = Resistor [tolerance=±5% resistance=150 package=THT]

nets:
  N1: Arduino1.D9_PWM, IC1.pin1, LED2.anode
  N2: Arduino1.D10_PWM/SS, IC1.pin2, LED1.anode
  N3: Arduino1.GND, IC1.pin4, C1.-, C2.1, R1.Pin_1
  N4: Arduino1.VIN, F1.1
  N5: IC1.pin3, J1.pin1
  N6: IC1.pin5, J1.pin2
  N7: IC1.pin7, F1.2, C1.+, C2.0
  N8: LED1.cathode, LED2.cathode, R1.Pin_0
