# Fritzing sketch PointControl (saved by Fritzing 0.9.2b)
breadboards: 1

parts:
  パーツ1 = Arduino Uno (Rev3)
  IC1 = IC, SIP package, 9 pins [chip_label=TA7291S]
  IC2 = IC, SIP package, 9 pins [chip_label=TA7291S]
  C1 = Ceramic Capacitor [capacitance=100nF package="100 mil [THT, multilayer]"]
  C2 = Ceramic Capacitor [capacitance=100nF package="100 mil [THT, multilayer]"]
  R1 = Resistor [tolerance=±5% resistance=150 package=THT]
  LED1 = LED - 5mm [color="Green (570nm)" package="5 mm [THT]"]
  LED2 = LED - 5mm [color="Red (633nm)" package="5 mm [THT]"]
  R2 = Resistor [tolerance=±5% resistance=150 package=THT]
  LED3 = LED - 5mm [color="Green (570nm)" package="5 mm [THT]"]
  LED4 = LED - 5mm [color="Red (633nm)" package="5 mm [THT]"]
  J1 = female pin header, 2 pins [form="♀ (female)"]
  J2 = female pin header, 2 pins [form="♀ (female)"]

nets:
  N1: パーツ1.A2, IC1.pin9, LED1.anode
  N2: パーツ1.A3, IC1.pin1, LED2.anode
  N3: パーツ1.A4/SDA, IC2.pin9, LED3.anode
  N4: パーツ1.A5/SCL, IC2.pin1, LED4.anode
  N5: パーツ1.GND, IC1.pin5, IC2.pin5, C1.0, C2.0, R1.Pin_1, R2.Pin_1
  N6: パーツ1.VIN, IC1.pin2, IC1.pin6, IC1.pin8, IC2.pin2, IC2.pin6, IC2.pin8, C1.1, C2.1
  N7: IC1.pin3, J1.pin2
  N8: IC1.pin7, J1.pin1
  N9: IC2.pin3, J2.pin2
  N10: IC2.pin7, J2.pin1
  N11: R1.Pin_0, LED1.cathode, LED2.cathode
  N12: R2.Pin_0, LED3.cathode, LED4.cathode
